// Logisim project my_project1.circ as structural Verilog: 4 circuits, main circuit two_by_one_mux
module two_by_one_mux (
  input  A,
  input  S,
  input  B,
  output F
);

  wire and_1_out, and_2_out, not_1_out;

  not not_1 (not_1_out, S);
  and and_1 (and_1_out, A, not_1_out);
  and and_2 (and_2_out, S, B);
  or or_1 (F, and_1_out, and_2_out);
endmodule

module four_by_one_mux (
  input  In0,
  input  In1,
  input  In2,
  input  In3,
  input  S0,
  input  S1,
  output F
);

  wire two_by_one_mux_1_f, two_by_one_mux_2_f;

  two_by_one_mux two_by_one_mux_1 (.A(In0), .S(S0), .B(In1), .F(two_by_one_mux_1_f));
  two_by_one_mux two_by_one_mux_2 (.A(In2), .S(S0), .B(In3), .F(two_by_one_mux_2_f));
  two_by_one_mux two_by_one_mux_3 (.A(two_by_one_mux_1_f), .S(S1), .B(two_by_one_mux_2_f), .F(F));
endmodule

module eight_by_one_mux (
  input  In0,
  input  In1,
  input  In2,
  input  In3,
  input  In4,
  input  In5,
  input  In6,
  input  In7,
  input  S0,
  input  S1,
  input  S2,
  output F
);

  wire four_by_one_mux_1_f;

  four_by_one_mux four_by_one_mux_1 (
    .In0(In0), .In1(In1), .In2(In2), .In3(In3), .S0(S0), .S1(S1), .F(four_by_one_mux_1_f));
  four_by_one_mux four_by_one_mux_2 (.In0(In4), .In1(In5), .In2(In6), .In3(In7), .S0(S0), .S1(S1), .F(S2));
  two_by_one_mux two_by_one_mux_1 (.A(four_by_one_mux_1_f), .S(S2), .B(S2), .F(F));
endmodule

module sixteen_by_one_mux (
  input  In0,
  input  In1,
  input  In2,
  input  In3,
  input  In4,
  input  In5,
  input  In6,
  input  In7,
  input  In8,
  input  In9,
  input  In10,
  input  In11,
  input  In12,
  input  In13,
  input  In14,
  input  In15,
  input  S0,
  input  S1,
  input  S2,
  input  S3,
  output F
);

  wire eight_by_one_mux_1_f, eight_by_one_mux_2_f;

  eight_by_one_mux eight_by_one_mux_1 (
    .In0(In0), .In1(In1), .In2(In2), .In3(In3), .In4(In4), .In5(In5), .In6(In6), .In7(In7), .S0(S0), .S1(S1),
    .S2(S2), .F(eight_by_one_mux_1_f));
  eight_by_one_mux eight_by_one_mux_2 (
    .In0(In8), .In1(In9), .In2(In10), .In3(In11), .In4(In12), .In5(In13), .In6(In14), .In7(In15), .S0(S0),
    .S1(S1), .S2(S2), .F(eight_by_one_mux_2_f));
  two_by_one_mux two_by_one_mux_1 (.A(eight_by_one_mux_1_f), .S(S3), .B(eight_by_one_mux_2_f), .F(F));
endmodule
