// Logisim project my_xor.circ as structural Verilog: 8 circuits, main circuit main
module main (
  input  X,
  input  Y,
  output X_XOR_Y
);

  wire and_1_out, and_2_out, not_1_out, not_2_out;

  not not_1 (not_1_out, X);
  not not_2 (not_2_out, Y);
  and and_1 (and_1_out, not_1_out, Y);
  and and_2 (and_2_out, X, not_2_out);
  or or_1 (X_XOR_Y, and_1_out, and_2_out);
endmodule

module onebittest_adder (
  input  A,
  input  B,
  input  Cin,
  output S,
  output Cout
);

  wire and_1_out, and_2_out, and_3_out, and_4_out, and_5_out, and_6_out, and_7_out, not_1_out, not_2_out,
       not_3_out;

  not not_1 (not_1_out, A);
  not not_2 (not_2_out, B);
  not not_3 (not_3_out, Cin);
  and and_1 (and_1_out, not_1_out, not_2_out, Cin);
  and and_2 (and_2_out, not_1_out, B, not_3_out);
  and and_3 (and_3_out, A, not_2_out, not_3_out);
  and and_4 (and_4_out, A, B, Cin);
  and and_5 (and_5_out, B, Cin);
  and and_6 (and_6_out, A, Cin);
  and and_7 (and_7_out, A, B);
  or or_1 (S, and_1_out, and_2_out, and_3_out, and_4_out);
  or or_2 (Cout, and_5_out, and_6_out, and_7_out);
endmodule

module twobit_adder (
  input  [1:0] A,
  input  [1:0] B,
  input  Cin,
  output [1:0] S,
  output Cout
);

  wire onebit_adder_1_cout;

  onebit_adder onebit_adder_1 (.A(A[0]), .B(B[0]), .Cin(Cin), .S(S[0]), .Cout(onebit_adder_1_cout));
  onebit_adder onebit_adder_2 (.A(A[1]), .B(B[1]), .Cin(onebit_adder_1_cout), .S(S[1]), .Cout(Cout));
endmodule

module fourbit_adder (
  input  [3:0] A,
  input  [3:0] B,
  input  Cin,
  output [3:0] S,
  output Cout
);

  wire twobit_adder_1_cout;

  // Probe on A[1:0]
  twobit_adder twobit_adder_1 (.A(A[1:0]), .B(B[1:0]), .Cin(Cin), .S(S[1:0]), .Cout(twobit_adder_1_cout));
  twobit_adder twobit_adder_2 (.A(A[3:2]), .B(B[3:2]), .Cin(twobit_adder_1_cout), .S(S[3:2]), .Cout(Cout));
endmodule

module eightbit_adder (
  input  [7:0] A,
  input  [7:0] B,
  input  Cin,
  output [7:0] S,
  output Cout
);

  wire fourbit_adder_1_cout;

  // Probe on A[3:0]
  fourbit_adder fourbit_adder_1 (.A(A[3:0]), .B(B[3:0]), .Cin(Cin), .S(S[3:0]), .Cout(fourbit_adder_1_cout));
  fourbit_adder fourbit_adder_2 (.A(A[7:4]), .B(B[7:4]), .Cin(fourbit_adder_1_cout), .S(S[7:4]), .Cout(Cout));
endmodule

module sixteenbit_adder (
  input  [15:0] A,
  input  [15:0] B,
  input  Cin,
  output [15:0] S,
  output Cout
);

  wire eightbit_adder_1_cout;

  // Probe on A[7:0]
  eightbit_adder eightbit_adder_1 (.A(A[7:0]), .B(B[7:0]), .Cin(Cin), .S(S[7:0]), .Cout(eightbit_adder_1_cout));
  eightbit_adder eightbit_adder_2 (.A(A[15:8]), .B(B[15:8]), .Cin(eightbit_adder_1_cout), .S(S[15:8]), .Cout(Cout));
endmodule

module onebit_adder (
  input  A,
  input  B,
  input  Cin,
  output S,
  output Cout
);

  wire and_1_out, and_2_out, xor_1_out;

  xor xor_1 (xor_1_out, A, B);
  xor xor_2 (S, xor_1_out, Cin);
  and and_1 (and_1_out, xor_1_out, Cin);
  and and_2 (and_2_out, A, B);
  or or_1 (Cout, and_1_out, and_2_out);
endmodule

module test_fourbit_adder (
  input  [3:0] A,
  input  Cin,
  input  [3:0] B,
  output [3:0] out_4,
  output out_5
);

  wire onebit_adder_1_cout, onebit_adder_2_cout, onebit_adder_3_cout;

  onebit_adder onebit_adder_1 (.A(A[0]), .B(B[0]), .Cin(Cin), .S(out_4[0]), .Cout(onebit_adder_1_cout));
  onebit_adder onebit_adder_2 (.A(A[1]), .B(B[1]), .Cin(onebit_adder_1_cout), .S(out_4[1]), .Cout(onebit_adder_2_cout));
  onebit_adder onebit_adder_3 (.A(A[2]), .B(B[2]), .Cin(onebit_adder_2_cout), .S(out_4[2]), .Cout(onebit_adder_3_cout));
  onebit_adder onebit_adder_4 (.A(A[3]), .B(B[3]), .Cin(onebit_adder_3_cout), .S(out_4[3]), .Cout(out_5));
endmodule
